# Fritzing sketch 4.1.Arduino按键去抖电路 (saved by Fritzing 0.9.5d)
breadboards: 1

parts:
  元件1 = Arduino Uno (Rev3)
  LED1 = LED - 3mm [color="Red (633nm)" package="3 mm [THT]"]
  S1 = Pushbutton [package="[THT]"]
  R1 = Resistor [tolerance=±5% resistance=220 package="2010 [SMD]"]

nets:
  N1: 元件1.D7, LED1.cathode, S1.Pin_1, S1.Pin_2, S1.Pin_3, S1.Pin_4, R1.Pin_0
  N2: 元件1.5V, LED1.anode
  N3: 元件1.GND, R1.Pin_1
